// Logisim project F3-2to4-decoder.circ as structural Verilog: 3 circuits, main circuit main
module main (
);

  decoder24 decoder24_1 ();  // open: in_1, in_2, Y0, Y1, Y2, Y3
  decoder24 decoder24_2 ();  // open: in_1, in_2, Y0, Y1, Y2, Y3
endmodule

module OR2 (
  input  A,
  input  B,
  output Y
);

  wire transistor_1_out, transistor_2_out;

  Transistor transistor_1 (.in(1'b1), .out(transistor_1_out), .gate(A));
  Transistor transistor_2 (.in(transistor_1_out), .out(transistor_2_out), .gate(B));
  Transistor #(.\type ("n")) transistor_3 (.in(1'b0), .out(transistor_2_out), .gate(A));
  Transistor #(.\type ("n")) transistor_4 (.in(1'b0), .out(transistor_2_out), .gate(B));
  Transistor transistor_5 (.in(1'b1), .out(Y), .gate(transistor_2_out));
  Transistor #(.\type ("n")) transistor_6 (.in(1'b0), .out(Y), .gate(transistor_2_out));
endmodule

module decoder24 (
  input  in_1,
  input  in_2,
  output Y0,
  output Y1,
  output Y2,
  output Y3
);

  wire transistor_1_out, transistor_3_out, transistor_5_out, transistor_6_out, transistor_7_out,
       transistor_9_out, transistor_11_out, transistor_12_out, transistor_14_out, transistor_15_out;

  Transistor transistor_1 (.in(1'b1), .out(transistor_1_out), .gate(in_1));
  Transistor #(.\type ("n")) transistor_2 (.in(1'b0), .out(transistor_1_out), .gate(in_1));
  Transistor transistor_3 (.in(1'b1), .out(transistor_3_out), .gate(in_2));
  Transistor #(.\type ("n")) transistor_4 (.in(1'b0), .out(transistor_3_out), .gate(in_2));
  Transistor transistor_5 (.in(1'b1), .out(transistor_5_out), .gate(transistor_1_out));
  Transistor transistor_6 (.in(1'b1), .out(transistor_6_out), .gate(in_1));
  Transistor #(.\type ("n")) transistor_7 (.in(1'b0), .out(transistor_7_out), .gate(transistor_1_out));
  Transistor #(.\type ("n")) transistor_8 (.in(transistor_7_out), .out(transistor_5_out), .gate(transistor_3_out));
  Transistor #(.\type ("n")) transistor_9 (.in(1'b0), .out(transistor_9_out), .gate(in_1));
  Transistor #(.\type ("n")) transistor_10 (.in(transistor_9_out), .out(transistor_6_out), .gate(transistor_3_out));
  Transistor #(.\type ("n")) transistor_11 (.in(1'b0), .out(transistor_11_out), .gate(transistor_1_out));
  Transistor #(.\type ("n")) transistor_12 (.in(transistor_11_out), .out(transistor_12_out), .gate(in_2));
  Transistor transistor_13 (.in(1'b1), .out(transistor_12_out), .gate(transistor_1_out));
  Transistor #(.\type ("n")) transistor_14 (.in(1'b0), .out(transistor_14_out), .gate(in_1));
  Transistor #(.\type ("n")) transistor_15 (.in(transistor_14_out), .out(transistor_15_out), .gate(in_2));
  Transistor transistor_16 (.in(1'b1), .out(transistor_15_out), .gate(in_1));
  Transistor transistor_17 (.in(1'b1), .out(transistor_5_out), .gate(transistor_3_out));
  Transistor transistor_18 (.in(1'b1), .out(transistor_6_out), .gate(transistor_3_out));
  Transistor transistor_19 (.in(1'b1), .out(transistor_12_out), .gate(in_2));
  Transistor transistor_20 (.in(1'b1), .out(transistor_15_out), .gate(in_2));
  Transistor transistor_21 (.in(1'b1), .out(Y0), .gate(transistor_5_out));
  Transistor #(.\type ("n")) transistor_22 (.in(1'b0), .out(Y0), .gate(transistor_5_out));
  Transistor transistor_23 (.in(1'b1), .out(Y1), .gate(transistor_6_out));
  Transistor #(.\type ("n")) transistor_24 (.in(1'b0), .out(Y1), .gate(transistor_6_out));
  Transistor transistor_25 (.in(1'b1), .out(Y2), .gate(transistor_12_out));
  Transistor #(.\type ("n")) transistor_26 (.in(1'b0), .out(Y2), .gate(transistor_12_out));
  Transistor transistor_27 (.in(1'b1), .out(Y3), .gate(transistor_15_out));
  Transistor #(.\type ("n")) transistor_28 (.in(1'b0), .out(Y3), .gate(transistor_15_out));
endmodule
